// Logisim project PIC16F84A.circ as structural Verilog: 12 circuits, main circuit PIC16F84A
module PIC16F84A (
  input  RB4,
  input  [3:0] RA3_0,
  input  [6:0] RB7_1,
  input  VDD_VSS,
  input  RB0_INT
);

  wire acc_w, call, clrwdt, comparator_1_eq, instruction_decode_1_instr_w, instruction_reg_1_skip_o,
       not_1_out, not_2_out, or_1_out, pop_t, push, push_t, RAM_r, RAM_w, reg_w, result_w, SEQ, skip, skip_e,
       sleep, WDT, wdt_t;
  wire [0:0] JMP_cmd;
  wire [1:0] CLK_RST, instruction_decode_1_step;
  wire [2:0] stack_counter_1_stack_pointer;
  wire [3:0] control, INT;
  wire [5:3] instruction_reg_1_instr_out_2;
  wire [6:0] multiplexer_1_out;
  wire [7:0] alu_1_output, controlled_buffer_1_out, EECON1, EECON1_out, FSR_reg, INTCON, INTCON_IN,
       multiplexer_2_out, OPT, ram_1_data_bus_out, register_1_q, register_2_q, ROM_out, TIMR0_INT,
       watchdog_1_wdt_timer;
  wire [10:0] instruction_reg_1_instr_out;
  wire [12:0] PCL_LATH, program_counter_1_program_counter, stack_counter_1_data_out;
  wire [13:0] rom_1_data;
  wire [15:0] ROM_in;
  wire [15:8] SFR_IN, SFRout;

  // Probe on instruction_reg_1_skip_o
  Instruction_reg instruction_reg_1 (
    .instr_w(instruction_decode_1_instr_w),
    .Instr_OUT({instruction_reg_1_instr_out_2, instruction_reg_1_instr_out}), .Instr_IN(rom_1_data),
    .CLK_RST(CLK_RST), .SKIP_o(instruction_reg_1_skip_o), .Skip(skip));
  Instruction_decode instruction_decode_1 (
    .CLK_RST(CLK_RST), .OPCODE({instruction_reg_1_instr_out_2, instruction_reg_1_instr_out[10:8]}),
    .SEQ(SEQ), .STEP(instruction_decode_1_step), .push(push), .pop(JMP_cmd[0]), .jmp(call),
    .result_w(result_w), .status_w(control[1]), .instr_w(instruction_decode_1_instr_w), .sleep(sleep),
    .clrwdt(clrwdt), .reg_w(reg_w), .ram_r(RAM_r), .skip_e(skip_e));
  Clock OSC1_CLKIN (.out(CLK_RST[0]));
  // Probe on rom_1_data
  // Probe on {instruction_reg_1_instr_out_2, instruction_reg_1_instr_out}
  // Probe on {instruction_reg_1_instr_out_2, instruction_reg_1_instr_out[10:8]}
  // Probe on instruction_decode_1_step
  // Probe on program_counter_1_program_counter
  ROM #(.addrWidth(13), .dataWidth(14)) rom_1 (
    .addr(program_counter_1_program_counter), .data(rom_1_data));  // open: sel
  Program_counter program_counter_1 (
    .INT(13'h4), .PROGRAM_COUNTER(program_counter_1_program_counter), .CLK_RST(CLK_RST), .SEQ(SEQ),
    .PCL_PCLATH(PCL_LATH), .Jump_cmd({1'b0, call, control[2], JMP_cmd[0]}),
    .GOTO(instruction_reg_1_instr_out), .STACK(stack_counter_1_data_out));
  // Probe on instruction_reg_1_instr_out
  Stack_counter stack_counter_1 (
    .PUSH(or_1_out), .POP(pop_t), .Stack_pointer(stack_counter_1_stack_pointer),
    .DATA_IN(program_counter_1_program_counter), .DATA_OUT(stack_counter_1_data_out), .CLK_RST(CLK_RST));
  or or_1 (or_1_out, push_t, control[2]);
  Watchdog watchdog_1 (
    .wdt(wdt_t), .SLEEP_CLRWDT({clrwdt, sleep}), .PD_TO(SFR_IN[12:11]), .WDT_CLK(WDT),
    .WDT_TIMER(watchdog_1_wdt_timer));
  // Probe on watchdog_1_wdt_timer
  Button MCLR (.out(CLK_RST[1]));
  // Probe on 13'h4
  // Probe on stack_counter_1_data_out
  // Probe on stack_counter_1_stack_pointer
  // Probe on PCL_LATH
  Interrupt interrupt_1 (.INT_W(control[2]), .INTCON_out(INTCON_IN), .INT_FLAGS(INT), .INTCON_in(INTCON));
  // Probe on instruction_reg_1_instr_out[7]
  and and_1 (acc_w, instruction_reg_1_instr_out[7], not_1_out);
  and and_2 (RAM_w, instruction_reg_1_instr_out[7], reg_w);
  // Probe on instruction_reg_1_instr_out[7]
  // Probe on {instruction_reg_1_instr_out_2, instruction_reg_1_instr_out[10:8]}
  not not_1 (not_1_out, reg_w);
  Comparator #(.width(7)) comparator_1 (
    .a({7{1'b0}}), .b(instruction_reg_1_instr_out[6:0]), .eq(comparator_1_eq));  // open: gt, lt
  // Probe on register_1_q
  // Probe on SFRout[10:8]
  Register register_1 (.D(register_2_q), .en(acc_w), .Q(register_1_q), .clk(CLK_RST[0]), .clr(CLK_RST[1]));
  RAM ram_1 (
    .DATA_BUS_OUT(ram_1_data_bus_out), .PC(PCL_LATH), .EEPROM_in({EECON1, ROM_in}),
    .SFR_OUT({OPT, INTCON, SFRout, FSR_reg}), .TIMR0_ctrl({INT, TIMR0_INT}), .Control_in({RB0_INT, control}),
    .EEPROM_out({EECON1_out, ROM_out}), .IO({RB0_INT, RB7_1, RB4, RA3_0}), .SFR_IN({SFR_IN, INTCON_IN}),
    .WE(RAM_w), .CLK_RST(CLK_RST), .ADDRESS(multiplexer_1_out), .DATA_BUS(controlled_buffer_1_out));
  // Probe on multiplexer_1_out
  Multiplexer #(.width(7), .enable("false")) multiplexer_1 (
    .in0(instruction_reg_1_instr_out[6:0]), .in1(FSR_reg[6:0]), .out(multiplexer_1_out), .sel(comparator_1_eq));
  // Probe on instruction_reg_1_instr_out[6:0]
  // Probe on FSR_reg[6:0]
  // Probe on instruction_reg_1_instr_out[7:0]
  // Probe on controlled_buffer_1_out
  // Probe on instruction_reg_1_instr_out_2[5]
  Multiplexer #(.width(8), .enable("false")) multiplexer_2 (
    .in0(instruction_reg_1_instr_out[7:0]), .in1(controlled_buffer_1_out), .out(multiplexer_2_out),
    .sel(instruction_reg_1_instr_out_2[5]));
  // Probe on multiplexer_2_out
  ALU alu_1 (
    .Z_DC_C(SFRout[10:8]), .DATA(multiplexer_2_out), .W(register_1_q), .OUTPUT(alu_1_output),
    .Z_DC_C_out(SFR_IN[10:8]), .Skip(skip), .OP_7(instruction_reg_1_instr_out[7]),
    .SEL({instruction_reg_1_instr_out_2, instruction_reg_1_instr_out[10:8]}));  // open: Control, Call_Goto, destf
  not not_2 (not_2_out, RAM_w);
  assign controlled_buffer_1_out = not_2_out ? ram_1_data_bus_out : 8'bz;  // Controlled_Buffer controlled_buffer_1
  // Probe on SFRout
  assign controlled_buffer_1_out = RAM_w ? register_2_q : 8'bz;  // Controlled_Buffer controlled_buffer_2
  Register #(.trigger("falling")) register_2 (
    .D(alu_1_output), .en(result_w), .Q(register_2_q), .clk(CLK_RST[0]), .clr(CLK_RST[1]));
  // Probe on controlled_buffer_1_out
  // Probe on ROM_in[7:0]
  // Probe on controlled_buffer_1_out
  EEPROM eeprom_1 (
    .EEDATA(ROM_in[7:0]), .EEADR(ROM_in[15:8]), .EECON_out(EECON1_out), .EEIF_out(control[3]),
    .EECON1(EECON1), .CLK_RST(CLK_RST), .EEDATA_out(ROM_out));
  // Probe on ROM_in[15:8]
  // Probe on TIMR0_INT
  Timing timing_1 (.SEQ(SEQ), .CLKI(RB4), .RST(CLK_RST[1]), .WDT(WDT), .rate(control[0]), .wdt_2(wdt_t), .OPT(OPT));
  // Probe on OPT
  LED led_1 (.in(control[3]));
  // Probe on EECON1_out
  // Probe on EECON1
  // Probe on ROM_out
  Clock T0CKI (.out(RB4));
  Button button_1 (.out(RB0_INT));

  // Other names for the same wires on the sheet: rst = CLK_RST[1]; tmr_w = control[0]; sw_w = control[1];
  //   EEIF = control[3]; IO[12:0] = {RB0_INT, RB7_1, RB4, RA3_0}; control[4] = RB0_INT; INTF = RB0_INT;
  //   pop = JMP_cmd[0]; int_w = control[2]; JMP_cmd[2:1] = {call, control[2]}; ROM_in[23:16] = EECON1;
  //   ROM_out[15:8] = EECON1_out; SFR_IN[7:0] = INTCON_IN; SW_IN[7:0] = SFR_IN;
  //   SFRout (some bits) = {OPT, INTCON, FSR_reg}; SW[7:0] = SFRout; TMR0[7:0] = TIMR0_INT; TIMR0_INT[11:8] = INT

  // Notes on the sheet:
  //   1K x 14
  //   Instruction
  //    Decode 
  //   & Control  
  //   Timing
  //   Flash Program
  //   Instruction reg
  //   contents of rom_1 (hex, n*v repeats v):
  //   0 1234 2bcd 3 4 5 6 7 8 9 a b c d e f
  //   Program counter
  //   8 level stack
  //   Control and signals
  //   Watchdog
  //   Interrupt
  //   INDF
  //   ALU
  //   W reg
  //   RAM
  //   RAM File 
  //   Registers
  //   68 x 8
  //   Result regster
  //   EEPROM
  //   EEPROM
  //   64x8
  //   TMR0
  //   IO ports
endmodule

module Program_counter (
  input  [3:0] Jump_cmd,
  input  [1:0] CLK_RST,
  input  SEQ,
  input  [12:0] STACK,
  input  [12:0] PCL_PCLATH,
  input  [10:0] GOTO,
  input  [12:0] INT,
  output [12:0] PROGRAM_COUNTER
);

  wire or_1_out;
  wire [1:0] priority_encoder_1_out;
  wire [12:0] multiplexer_1_out;

  // Probe on Jump_cmd[0]
  // Probe on Jump_cmd[1]
  // Probe on Jump_cmd[2]
  // Probe on Jump_cmd[3]
  or or_1 (or_1_out, Jump_cmd[0], Jump_cmd[1], Jump_cmd[2], Jump_cmd[3]);
  Priority_Encoder #(.select(2)) priority_encoder_1 (
    .in0(Jump_cmd[0]), .in1(Jump_cmd[1]), .in2(Jump_cmd[2]), .in3(Jump_cmd[3]), .out(priority_encoder_1_out));  // open: gs, en_out, en_in
  // Probe on or_1_out
  // Probe on multiplexer_1_out
  // Probe on multiplexer_1_out
  Multiplexer #(.select(2), .width(13), .enable("false")) multiplexer_1 (
    .in0(STACK), .in1(INT), .in2({PCL_PCLATH[12:11], GOTO}), .in3(PCL_PCLATH), .out(multiplexer_1_out),
    .sel(priority_encoder_1_out));
  // Probe on priority_encoder_1_out
  // Probe on STACK
  // Probe on INT
  Counter #(.width(13), .max('h1fff)) PC (
    .load(or_1_out), .D(multiplexer_1_out), .count(SEQ), .Q(PROGRAM_COUNTER), .clk(CLK_RST[0]),
    .clr(CLK_RST[1]));  // open: carry
  // Probe on PCL_PCLATH
  // Probe on {PCL_PCLATH[12:11], GOTO}
endmodule

module Stack_counter (
  input  [12:0] DATA_IN,
  input  PUSH,
  input  [1:0] CLK_RST,
  input  POP,
  output [2:0] Stack_pointer,
  output [12:0] DATA_OUT
);

  wire and_1_out, not_1_out, not_2_out, or_1_out, subtractor_1_bout;
  wire [2:0] adder_1_out, controlled_buffer_1_out, multiplexer_1_out, subtractor_1_out;

  Adder #(.width(3)) adder_1 (.a(Stack_pointer), .b({2'b00, PUSH}), .out(adder_1_out), .cin(1'b0));  // open: cout
  and and_1 (and_1_out, POP, not_1_out);
  Subtractor #(.width(3)) subtractor_1 (
    .a(Stack_pointer), .b({2'b00, POP}), .out(subtractor_1_out), .bin(1'b0), .bout(subtractor_1_bout));
  not not_1 (not_1_out, subtractor_1_bout);
  or or_1 (or_1_out, PUSH, and_1_out);
  assign controlled_buffer_1_out = PUSH ? adder_1_out : 3'bz;  // Controlled_Buffer controlled_buffer_1
  assign controlled_buffer_1_out = POP ? subtractor_1_out : 3'bz;  // Controlled_Buffer controlled_buffer_2
  Register #(.width(3)) register_1 (
    .D(controlled_buffer_1_out), .en(or_1_out), .Q(Stack_pointer), .clk(CLK_RST[0]), .clr(CLK_RST[1]));
  // Probe on Stack_pointer
  Multiplexer #(.width(3), .enable("false")) multiplexer_1 (
    .in0(Stack_pointer), .in1(adder_1_out), .out(multiplexer_1_out), .sel(PUSH));
  RAM #(.addrWidth(3), .dataWidth(13)) ram_1 (
    .addr(multiplexer_1_out), .data(DATA_OUT), .sel(1'b1), .clk(CLK_RST[0]), .ld(not_2_out), .clr(CLK_RST[1]));
  not not_2 (not_2_out, PUSH);
  assign DATA_OUT = PUSH ? DATA_IN : 13'bz;  // Controlled_Buffer controlled_buffer_3

  // Other names for the same wires on the sheet: SP[2:0] = Stack_pointer
endmodule

module Instruction_decode (
  input  [5:0] OPCODE,
  input  [1:0] CLK_RST,
  output push,
  output pop,
  output jmp,
  output skip_e,
  output ram_r,
  output result_w,
  output status_w,
  output reg_w,
  output clrwdt,
  output sleep,
  output [1:0] STEP,
  output SEQ,
  output instr_w
);

  wire comparator_1_eq;

  Counter #(.width(2), .max('h3)) counter_1 (
    .Q(STEP), .carry(SEQ), .clk(CLK_RST[0]), .clr(CLK_RST[1]));  // open: load, D, count
  Comparator #(.width(2)) comparator_1 (.a(STEP), .b(2'b00), .eq(comparator_1_eq));  // open: gt, lt
  and and_1 (instr_w, comparator_1_eq, CLK_RST[0]);
  ROM #(.dataWidth(10)) rom_1 (
    .addr({OPCODE, STEP}), .data({sleep, clrwdt, reg_w, status_w, result_w, ram_r, skip_e, jmp, pop, push}),
    .sel(1'b1));

  // Notes on the sheet:
  //   Sequencer
endmodule

module InstructionDecode (
  input  [5:0] OPCODE,
  input  [1:0] CLK_RST,
  output push,
  output pop,
  output jmp,
  output skip_e,
  output ram_r,
  output result_w,
  output status_w,
  output reg_w,
  output clrwdt,
  output sleep,
  output [1:0] STEP,
  output SEQ,
  output instr_w
);

  wire comparator_1_eq, counter_1_carry;
  wire [1:0] counter_1_q;
  wire [9:0] rom_1_data;

  Counter #(.width(2), .max('h3)) counter_1 (
    .Q(counter_1_q), .carry(counter_1_carry), .clk(CLK_RST[0]), .clr(CLK_RST[1]));  // open: load, D, count
  Comparator #(.width(2)) comparator_1 (.a(counter_1_q), .b(2'b00), .eq(comparator_1_eq));  // open: gt, lt
  and and_1 (instr_w, comparator_1_eq, CLK_RST[0]);
  ROM #(.dataWidth(10)) rom_1 (.addr({OPCODE, counter_1_q}), .data(rom_1_data), .sel(1'b1));

  // Notes on the sheet:
  //   Sequencer
endmodule

module Instruction_reg (
  input  [13:0] Instr_IN,
  input  Skip,
  input  instr_w,
  input  [1:0] CLK_RST,
  output SKIP_o,
  output [13:0] Instr_OUT
);

  wire and_1_out, d_ff_1_qn, not_1_out;
  wire [13:0] multiplexer_1_out;

  and and_1 (and_1_out, Skip, not_1_out);
  not not_1 (not_1_out, instr_w);
  D_Flip_Flop #(.trigger("falling")) d_ff_1 (
    .clk(CLK_RST[0]), .D(not_1_out), .Q(SKIP_o), .Qn(d_ff_1_qn), .preset(and_1_out), .en(instr_w));  // open: reset
  // Probe on Instr_IN
  Multiplexer #(.width(14), .disabled(0), .enable("false")) multiplexer_1 (
    .in0({14{1'b0}}), .in1(Instr_IN), .out(multiplexer_1_out), .sel(d_ff_1_qn));
  // Probe on multiplexer_1_out
  Register #(.width(14), .trigger("falling")) register_1 (
    .D(multiplexer_1_out), .en(instr_w), .Q(Instr_OUT), .clk(CLK_RST[0]), .clr(CLK_RST[1]));
endmodule

module Interrupt (
  input  [3:0] INT_FLAGS,
  input  [7:0] INTCON_in,
  output INT_W,
  output [7:0] INTCON_out
);

  wire and_2_out, and_3_out, and_4_out, and_5_out, or_1_out;

  or or_1 (or_1_out, and_2_out, and_3_out, and_4_out, and_5_out);
  and and_1 (INT_W, or_1_out, INTCON_in[7]);
  and and_2 (and_2_out, INT_FLAGS[0], INTCON_in[3]);
  and and_3 (and_3_out, INT_FLAGS[1], INTCON_in[4]);
  and and_4 (and_4_out, INT_FLAGS[2], INTCON_in[5]);
  and and_5 (and_5_out, INT_FLAGS[3], INTCON_in[6]);
  // Probe on INTCON_in[7:3]
  // Probe on INT_FLAGS[0]
  // Probe on INT_FLAGS[1]
  // Probe on INT_FLAGS[2]
  // Probe on INT_FLAGS[3]
  assign INTCON_out[7:3] = INTCON_in[7:3];  // Buffer buffer_1, 5 bits wide

  assign INTCON_out[2:0] = INT_FLAGS[2:0];

  // Notes on the sheet:
  //   Interrupt Handling
endmodule

module EEPROM (
  input  [7:0] EEDATA,
  input  [7:0] EEADR,
  input  [7:0] EECON1,
  input  [1:0] CLK_RST,
  output [7:0] EEDATA_out,
  output EEIF_out,
  output [7:0] EECON_out
);

  wire and_1_out, not_1_out, or_1_out;
  wire [7:0] ram_1_data;

  // Probe on EEADR
  not not_1 (not_1_out, and_1_out);
  or or_1 (or_1_out, EECON1[0], and_1_out);
  and and_1 (and_1_out, EECON1[2], EECON1[1]);
  // Probe on ram_1_data
  RAM ram_1 (.addr(EEADR), .data(ram_1_data), .sel(or_1_out), .clk(CLK_RST[0]), .ld(not_1_out), .clr(CLK_RST[1]));
  Multiplexer #(.width(8), .enable("false")) multiplexer_1 (
    .in0(EEDATA), .in1(EEDATA_out), .out(ram_1_data), .sel(and_1_out));
  Counter #(.width(2), .max('h3)) counter_1 (
    .count(and_1_out), .carry(EECON_out[4]), .clk(CLK_RST[0]), .clr(CLK_RST[1]));  // open: load, D, Q
  assign EECON_out[3:2] = EECON1[3:2];  // Buffer buffer_1, 2 bits wide

  assign {EECON_out[7:5], EECON_out[1:0]} = {5{1'b0}};
  assign EEIF_out = EECON_out[4];

  // Other names for the same wires on the sheet: WREN = EECON1[2]; WRERR = EECON1[3]; RD = EECON1[0]; WR = EECON1[1];
  //   EEIF = EECON1[4]
endmodule

module Timing (
  input  SEQ,
  input  CLKI,
  input  [7:0] OPT,
  input  RST,
  input  WDT,
  output rate,
  output wdt_2
);

  wire multiplexer_1_out, multiplexer_2_out, prescsaler_1_rate, xor_1_out;
  wire [7:0] prescsaler_1_prs_count;

  Clock #(.lowDuration(3)) clock_1 ();  // open: out
  Clock clock_2 ();  // open: out
  // Probe on OPT[3]
  // Probe on OPT[5]
  // Probe on OPT[4]
  Button button_1 ();  // open: out
  Clock clock_3 ();  // open: out
  xor xor_1 (xor_1_out, CLKI, OPT[4]);
  // Probe on OPT[4]
  Multiplexer #(.enable("false")) multiplexer_1 (.in0(SEQ), .in1(xor_1_out), .out(multiplexer_1_out), .sel(OPT[5]));
  // Probe on OPT[5]
  // Probe on OPT[2:0]
  // Probe on OPT[3]
  Multiplexer #(.enable("false")) multiplexer_2 (
    .in0(multiplexer_1_out), .in1(WDT), .out(multiplexer_2_out), .sel(OPT[3]));
  Prescsaler prescsaler_1 (
    .PSA(OPT[2:0]), .CLK(multiplexer_2_out), .RST(RST), .rate(prescsaler_1_rate),
    .prs_count(prescsaler_1_prs_count));
  // Probe on prescsaler_1_prs_count
  Multiplexer #(.enable("false")) multiplexer_3 (
    .in0(prescsaler_1_rate), .in1(multiplexer_1_out), .out(rate), .sel(OPT[3]));
  Multiplexer #(.enable("false")) multiplexer_4 (.in0(WDT), .in1(prescsaler_1_rate), .out(wdt_2), .sel(OPT[3]));

  // Notes on the sheet:
  //   PRESCALER
endmodule

module Watchdog (
  input  wdt,
  input  [1:0] SLEEP_CLRWDT,
  output [1:0] PD_TO,
  output [7:0] WDT_TIMER,
  output WDT_CLK
);

  wire button_1_out, button_2_out, counter_1_carry;

  // Probe on SLEEP_CLRWDT[1]
  // Probe on SLEEP_CLRWDT[0]
  D_Flip_Flop d_ff_1 (.Qn(PD_TO[0]), .preset(SLEEP_CLRWDT[0]), .reset(SLEEP_CLRWDT[1]));  // open: clk, D, Q, en
  Button button_1 (.out(button_1_out));
  Button button_2 (.out(button_2_out));
  // Probe on PD_TO[0]
  // Probe on PD_TO[1]
  not not_1 (PD_TO[1], counter_1_carry);
  Counter counter_1 (
    .count(wdt), .Q(WDT_TIMER), .carry(counter_1_carry), .clk(WDT_CLK), .clr(SLEEP_CLRWDT[1]));  // open: load, D
  Clock #(.highDuration(2), .lowDuration(2)) u_WDT (.out(WDT_CLK));
endmodule

module Prescsaler (
  input  [2:0] PSA,
  input  CLK,
  input  RST,
  output [7:0] prs_count,
  output rate
);

  wire comparator_1_eq, comparator_2_eq, not_1_out, not_2_out, or_1_out;
  wire [1:0] clock_1_out;
  wire [2:0] register_1_q;
  wire [7:0] multiplexer_1_out;

  Clock clock_1 (.out(clock_1_out[0]));
  Button button_1 (.out(clock_1_out[1]));
  Register #(.width(3)) register_1 (.D(PSA), .en(not_1_out), .Q(register_1_q), .clk(CLK), .clr(RST));
  not not_1 (not_1_out, comparator_1_eq);
  or or_1 (or_1_out, not_1_out, comparator_2_eq);
  Comparator #(.width(3)) comparator_1 (.a(PSA), .b(register_1_q), .eq(comparator_1_eq));  // open: gt, lt
  Multiplexer #(.select(3), .width(8), .enable("false")) multiplexer_1 (
    .in0(8'h1), .in1(8'h3), .in2(8'h7), .in3(8'hf), .in4(8'h1f), .in5(8'h3f), .in6(8'h7f), .in7({8{1'b1}}),
    .out(multiplexer_1_out), .sel(PSA));
  Counter counter_1 (
    .load(or_1_out), .D({8{1'b0}}), .count(not_2_out), .Q(prs_count), .clk(CLK), .clr(RST));  // open: carry
  not not_2 (not_2_out, or_1_out);
  // Probe on multiplexer_1_out
  Comparator comparator_2 (.a(prs_count), .b(multiplexer_1_out), .eq(comparator_2_eq));  // open: gt, lt
  and and_1 (rate, CLK, comparator_2_eq);
endmodule

module tester (
);

  wire comparator_1_eq, instruction_reg_1_skip_o, Skip_e_out;
  wire [1:0] clock_1_out, counter_1_q;
  wire [13:0] counter_2_q, instruction_reg_1_instr_out;

  Counter #(.width(2), .max('h3)) counter_1 (
    .Q(counter_1_q), .clk(clock_1_out[0]), .clr(clock_1_out[1]));  // open: load, D, count, carry
  Comparator #(.width(2)) comparator_1 (.a(counter_1_q), .b(2'b00), .eq(comparator_1_eq));  // open: gt, lt
  Button button_1 (.out(clock_1_out[1]));
  Clock clock_1 (.out(clock_1_out[0]));
  Button Skip_e (.out(Skip_e_out));
  Instruction_reg instruction_reg_1 (
    .instr_w(comparator_1_eq), .Instr_OUT(instruction_reg_1_instr_out), .Instr_IN(counter_2_q),
    .CLK_RST(clock_1_out), .SKIP_o(instruction_reg_1_skip_o), .Skip(Skip_e_out));
  Counter #(.width(14), .max('h3fff)) counter_2 (
    .Q(counter_2_q), .clk(clock_1_out[0]), .clr(clock_1_out[1]));  // open: load, D, count, carry
  // Probe on instruction_reg_1_skip_o
  // Probe on instruction_reg_1_instr_out
endmodule
